// Digital circuit ι.dig as structural Verilog
module \ι  (
  input  [63:0] _64_127,
  input  [63:0] _128_191,
  input  [63:0] _191_255,
  input  [63:0] _0_63,
  output [63:0] _0_63_2,
  output [63:0] _64_127_2,
  output [63:0] _128_191_2,
  output [63:0] _192_255
);

  xor xor_1 (_0_63_2[0], _0_63[0], 1'b1);

  assign _0_63_2[63:1] = _0_63[63:1];
  assign _64_127_2 = _64_127;
  assign _128_191_2 = _128_191;
  assign _192_255 = _191_255;
endmodule
